// Logisim project counter.circ as structural Verilog: 1 circuit, main circuit main
module main (
);

  wire and_1_out, and_2_out, and_3_out, clock_1_out;
  wire [3:0] t_ff_4_q;

  Clock clock_1 (.out(clock_1_out));
  and and_1 (and_1_out, 1'b1, t_ff_4_q[0], t_ff_4_q[1], t_ff_4_q[2]);
  and and_2 (and_2_out, 1'b1, t_ff_4_q[0], t_ff_4_q[1]);
  and and_3 (and_3_out, 1'b1, t_ff_4_q[0]);
  T_Flip_Flop t_ff_1 (.clk(clock_1_out), .T(and_1_out), .Q(t_ff_4_q[3]));  // open: Qn, preset, reset, en
  T_Flip_Flop t_ff_2 (.clk(clock_1_out), .T(and_2_out), .Q(t_ff_4_q[2]));  // open: Qn, preset, reset, en
  T_Flip_Flop t_ff_3 (.clk(clock_1_out), .T(and_3_out), .Q(t_ff_4_q[1]));  // open: Qn, preset, reset, en
  T_Flip_Flop t_ff_4 (.clk(clock_1_out), .T(1'b1), .Q(t_ff_4_q[0]));  // open: Qn, preset, reset, en
  // Probe on t_ff_4_q
endmodule
